# Fritzing sketch esquematico_standalone (saved by Fritzing 0.8.7b)
breadboards: 1

parts:
  Part1 = Arduino Uno (Rev3)
  R1 = Resistor [tolerance=±5% resistance=220 package=THT]
  Q1 = NPN-Transistor [package="TO92 [THT]"]
  Q2 = NPN-Transistor [package="TO92 [THT]"]
  VCC1 = Battery block 9V
  M1 = DC Motor
  M2 = DC Motor
  S1 = Pushbutton [package="[THT]"]
  S2 = Pushbutton [package="[THT]"]
  R2 = Resistor [tolerance=±5% resistance=220 package=THT]
  R3 = Resistor [tolerance=±5% resistance=220 package=THT]

nets:
  N1: Part1.GND, VCC1.-, M1.pin_2, M2.pin_2, R2.Pin_1, R3.Pin_1
  N2: Part1.D2, R1.Pin_0
  N3: Part1.D3_PWM, Q2.B
  N4: Part1.D4, Q1.B
  N5: Part1.D5_PWM, S2.Pin_3, S2.Pin_4, R3.Pin_0
  N6: Part1.D6_PWM, S1.Pin_3, S1.Pin_4, R2.Pin_0
  N7: Part1.5V, Q1.C, Q2.C, S1.Pin_1, S1.Pin_2, S2.Pin_1, S2.Pin_2
  N8: Part1.VIN, VCC1.+
  N9: Q1.E, M1.pin_1
  N10: Q2.E, M2.pin_1
